// Logisim project alu.circ as structural Verilog: 2 circuits, main circuit alu
module alu (
  input  [31:0] A,
  input  [31:0] B,
  input  [3:0] ALUSel,
  output [31:0] Result
);

  wire [4:0] undriven, undriven_2, undriven_3;
  wire [31:0] add, \and , div, mulh, mulhu, mult, \or , rem, sll, slt, sra, srl, sub, \xor ;

  Adder #(.width(32)) adder_1 (.a(A), .b(B), .out(add));  // open: cin, cout
  assign \and  = A;  // AND_Gate and_1, 32 bits wide AND_Gate
  assign \or  = B;  // OR_Gate or_1, 32 bits wide OR_Gate
  assign \xor  = A ^ B;  // XOR_Gate xor_1, 32 bits wide
  Shifter #(.width(32), .shift("lr")) shifter_1 (.in(A), .\dist (undriven_2), .out(srl));
  Shifter #(.width(32), .shift("lr")) shifter_2 (.in(A), .out(sra));  // open: dist
  Shifter #(.width(32)) shifter_3 (.in(A), .\dist (undriven_3), .out(sll));
  Shifter #(.width(32)) shifter_4 (.in(A), .\dist (undriven), .out(slt));
  Divider #(.width(32)) divider_1 (.a(A), .b(B), .out(div), .rem(rem));  // open: upper
  Multiplier #(.width(32)) multiplier_1 (.a(A), .b(B), .out(mult));  // open: cin, cout
  Subtractor #(.width(32)) subtractor_1 (.a(A), .b(B), .out(sub));  // open: bin, bout
  Multiplexer #(.select(4), .width(32), .enable("false")) multiplexer_1 (
    .in0(add), .in1(\and ), .in2(\or ), .in3(\xor ), .in4(srl), .in5(sra), .in6(sll), .in7(slt), .in8(div),
    .in9(rem), .in10(mult), .in11(mulhu), .in12(sub), .in13(B), .in14(mulh), .out(Result), .sel(ALUSel));  // open: in15

  // Notes on the sheet:
  //   INPUTS to your circuit
  //   DON'T CHANGE THE LOCATIONS OF THE INPUTS AND OUTPUTS!
  //   OUTPUT from your circuit
endmodule

module div (
  input  [31:0] in_1,
  input  [31:0] in_2,
  output [31:0] out_3,
  output [31:0] out_4
);

  Divider #(.width(32)) divider_1 (.a(in_1), .b(in_2), .out(out_3), .rem(out_4));  // open: upper
endmodule
